# Fritzing sketch project-atlantics (saved by Fritzing 0.9.3b)

parts:
  Raspberry_Pi_1 = Raspberry Pi 3 [part_number=RPI-3-V1.2]
  8_Channel_Relay1 = 8 Channel Power Relay
  RHT1 = Humidity and Temperature Sensor RHT03
  Part1 = Arduino Nano (Rev3.0)
  Part2 = Soil Moisture Sensor
  S1 = PH meter [package=THT]
  Part3 = LCD1602-I2C

nets:
  3V3: Raspberry_Pi_1.3v3, RHT1.Vcc
  N1: Raspberry_Pi_1.GPIO2, Part3.GND
  N2: Raspberry_Pi_1.GIPO4, RHT1.Data-signal
  GND: Raspberry_Pi_1.GND, Raspberry_Pi_1.GIPO26, 8_Channel_Relay1.GND, RHT1.GND_1
  N3: Raspberry_Pi_1.GIPO17, 8_Channel_Relay1.IN1
  N4: Raspberry_Pi_1.GIPO27, 8_Channel_Relay1.IN2
  N5: Raspberry_Pi_1.GIPO5, 8_Channel_Relay1.IN6
  N6: Raspberry_Pi_1.GIPO6, 8_Channel_Relay1.IN7
  N7: Raspberry_Pi_1.GIPO20, 8_Channel_Relay1.IN8
  N8: Raspberry_Pi_1.GIPO25, 8_Channel_Relay1.IN5
  N9: Raspberry_Pi_1.GIPO24, 8_Channel_Relay1.IN4
  N10: Raspberry_Pi_1.GIPO23, 8_Channel_Relay1.IN3
  N11: Raspberry_Pi_1.GIPO15, Part1.D1/TX
  N12: Raspberry_Pi_1.GIPO14, Part1.D0/RX
  VCC: Raspberry_Pi_1.5V, 8_Channel_Relay1.VCC, Part3.VCC
  GND_2: Part1.GND, Part2.GND
  5V: Part1.5V, Part2.VCC
  N13: Part1.A1, S1.pin1
  N14: Part1.A0, Part2.SIG

custom parts:
  8 Channel Power Relay: An 8 channel power relay. The module operates at 5V.
  LCD1602-I2C: A standard character display, usually with 2x16 characters. Comes in many colors with LCM1602 IIC attached.
